# Fritzing sketch laser with photocell and button (saved by Fritzing 0.9.3b)
breadboards: 1

parts:
  Part1 = Arduino Uno (Rev3)
  R1 = Photocell (LDR) [package=THT]
  S1 = Pushbutton [package="[THT]"]
  Part2 = Ambient Light Sensor (TEMT6000 Breakout Board)
  R2 = Resistor [tolerance=±5% resistance=10k package="2010 [SMD]"]
  R3 = Resistor [tolerance=±5% resistance=10k package="2010 [SMD]"]
  Part3 = Ambient Light Sensor (TEMT6000 Breakout Board)  # not connected

nets:
  N1: Part1.A0, R1.pin_1, R2.Pin_0
  N2: Part1.D13/SCK, Part2.S
  GND: Part1.GND, R1.pin_0, Part2.GND, R3.Pin_1
  N3: Part1.D2, S1.Pin_1, S1.Pin_2, R3.Pin_0
  5V: Part1.5V, S1.Pin_3, S1.Pin_4, Part2.VCC, R2.Pin_1

notes:
  This is a laser
